# Fritzing sketch BASE (saved by Fritzing 1.0.6)
breadboards: 3

parts:
  microSD1 = MicroSD Card Module
  ZS-042_RTC1 = ZS-042 RTC Module
  Componente1 = Arduino Uno (Rev3) - ICSP
  Componente8 = LCD1602-I2C
  Componente9 = Arduino Uno (Rev3) - ICSP
  Componente10 = LCD1602-I2C
  Componente11 = Arduino Uno (Rev3) - ICSP
  Componente12 = LCD1602-I2C
  ZS-042_RTC2 = ZS-042 RTC Module

nets:
  N1: microSD1.MISO, Componente1.D12/MISO
  N2: microSD1.MOSI, Componente1.D11_PWM/MOSI
  N3: microSD1.SCK, Componente1.D13/SCK
  N4: microSD1.CS, Componente1.D10_PWM/SS
  GND: ZS-042_RTC1.GND, Componente1.GND, Componente8.GND
  VCC: ZS-042_RTC1.VCC, Componente1.5V, Componente8.VCC
  N5: ZS-042_RTC1.SDA, Componente1.A4/SDA, Componente8.SDA
  N6: ZS-042_RTC1.SCL, Componente1.A5/SCL, Componente8.SCL
  N7: Componente9.A4/SDA, Componente10.SDA
  N8: Componente9.A5/SCL, Componente10.SCL
  5V: Componente9.5V, Componente10.VCC
  GND_2: Componente9.GND, Componente10.GND
  N9: Componente11.A4/SDA, Componente12.SDA, ZS-042_RTC2.SDA
  N10: Componente11.A5/SCL, Componente12.SCL, ZS-042_RTC2.SCL
  VCC_2: Componente11.5V, Componente12.VCC, ZS-042_RTC2.VCC
  GND_3: Componente11.GND, Componente12.GND, ZS-042_RTC2.GND

custom parts:
  LCD1602-I2C: A standard character display, usually with 2x16 characters. Comes in many colors with LCM1602 IIC attached.
