# Fritzing sketch Potes y Leds (saved by Fritzing 1.0.6)
breadboards: 2

parts:
  Componente1 = Arduino Uno (Rev3) - ICSP
  S1 = Pushbutton [package="[THT]"]
  LED1 = LED - 5mm [color="Red (633nm)" current=0.030A package="5 mm [THT]"]
  R1 = Resistor [tolerance=±5% resistance=220 package="0402 [SMD]"]
  R2 = Rotary Potentiometer (Small) [maximum_resistance=10kΩ knob_status=50% power=0.5W package=THT]
  LED2 = LED - 5mm [color="Green (555nm)" current=0.030A package="5 mm [THT]"]
  LED3 = LED - 5mm [color="Blue (470nm)" current=0.030A package="5 mm [THT]"]
  R3 = Resistor [tolerance=±5% resistance=220 package="0402 [SMD]"]
  R4 = Resistor [tolerance=±5% resistance=220 package="0402 [SMD]"]
  A1 = AHT10 module
  Componente2 = Arduino Uno (Rev3) - ICSP
  LED4 = LED - 5mm [color="Red (633nm)" current=0.030A package="5 mm [THT]"]
  Componente3 = Arduino Uno (Rev3) - ICSP
  S2 = Pushbutton [package="[THT]"]
  LED6 = LED - 5mm [color="Red (633nm)" current=0.030A package="5 mm [THT]"]
  R6 = Resistor [tolerance=±5% resistance=220 package="0402 [SMD]"]

nets:
  N1: Componente1.A0, R2.wiper
  N2: Componente1.5V, R2.leg1
  N3: Componente1.GND, S1.Pin_3, S1.Pin_4, LED1.cathode, R2.leg2, LED2.cathode, LED3.cathode
  N4: Componente1.D2, S1.Pin_1, S1.Pin_2
  N5: Componente1.D3_PWM, R1.Pin_1
  N6: Componente1.D4, R4.Pin_1
  N7: Componente1.D5_PWM, R3.Pin_1
  N8: LED1.anode, R1.Pin_0
  N9: LED2.anode, R3.Pin_0
  N10: LED3.anode, R4.Pin_0
  N11: A1.Pin_1, Componente2.A5/SCL
  N12: A1.Pin_2, Componente2.A4/SDA
  N13: A1.Pin_3, Componente2.GND, LED4.cathode
  N14: A1.Pin_4, Componente2.5V
  N15: Componente2.D13/SCK, LED4.anode
  N16: Componente3.GND, S2.Pin_3, S2.Pin_4, LED6.cathode
  N17: Componente3.D2, S2.Pin_1, S2.Pin_2
  N18: Componente3.D3_PWM, R6.Pin_1
  N19: LED6.anode, R6.Pin_0

custom parts:
  AHT10 module: AHT10 Temperature Humidity Sensor Measurement Module High-Precision Digital Temp Humidity Sensor Measurement Module 1.8-6.0V I2C.
