# Fritzing sketch ARQ (saved by Fritzing 1.0.6)
breadboards: 1

parts:
  PIR1 = PIR sensor
  Mod1 = MQ-7 breakout
  Componente7 = BH1750
  A1 = AHT10 module
  Componente5 = Breakout Board for Electret Microphone
  Mod2 = MQ-7 breakout
  Componente11 = Arduino Uno (Rev3) - ICSP
  Componente12 = LCD1602-I2C
  microSD3 = MicroSD Card Module
  ZS-042_RTC3 = ZS-042 RTC Module

nets:
  VCC: PIR1.VDD, Mod1.VCC, Componente7.VCC, A1.Pin_4, Componente5.VCC, Mod2.VCC, Componente11.5V, Componente12.VCC, ZS-042_RTC3.VCC
  N1: PIR1.SIG, Componente11.D2
  GND: PIR1.GND, Mod1.GND, Componente7.GND, A1.Pin_3, Componente5.GND, Mod2.GND, Componente11.GND, Componente12.GND, ZS-042_RTC3.GND
  N2: Mod1.DO, Componente11.A1
  N3: Componente7.SCL, A1.Pin_1, Componente11.A5/SCL, Componente12.SCL, ZS-042_RTC3.SCL
  N4: Componente7.SDA, A1.Pin_2, Componente11.A4/SDA, Componente12.SDA, ZS-042_RTC3.SDA
  N5: Componente5.AUD, Componente11.A2
  N6: Mod2.DO, Componente11.A0
  N7: Componente11.D10_PWM/SS, microSD3.CS
  N8: Componente11.D11_PWM/MOSI, microSD3.MOSI
  N9: Componente11.D12/MISO, microSD3.MISO
  N10: Componente11.D13/SCK, microSD3.SCK

custom parts:
  MQ-7 breakout: MQ-5 gas sensor
  BH1750: Light Sensor
  AHT10 module: AHT10 Temperature Humidity Sensor Measurement Module High-Precision Digital Temp Humidity Sensor Measurement Module 1.8-6.0V I2C.
  LCD1602-I2C: A standard character display, usually with 2x16 characters. Comes in many colors with LCM1602 IIC attached.
