# Fritzing sketch H2O (saved by Fritzing 1.0.6)
breadboards: 1

parts:
  A2 = tds-sensor-meter-v1.0_1
  U1 = Turbidity Sensor Probe [package=THT]
  U2 = DFRobot SEN0189 [package=THT]
  DS1 = DS18B20 1-Wire Temperature Sensor Probe
  pH_Circuit1 = pH Circuit
  Conductivity_Circuit1 = Conductivity Circuit
  D_O_Circuit1 = D.O. Circuit
  Componente9 = Arduino Uno (Rev3) - ICSP
  Componente10 = LCD1602-I2C
  microSD2 = MicroSD Card Module
  ZS-042_RTC2 = ZS-042 RTC Module

nets:
  N1: A2.pin1, Componente9.A1
  N2: A2.pin2, U2.P1_2
  N3: A2.pin3, U2.P1_3
  N4: U1.pin1, U2.P2_3
  N5: U1.pin2, U2.P2_2
  N6: U1.VCC, U2.P2_1
  N7: U2.P1_1, Componente9.A0
  GND: DS1.GND, pH_Circuit1.GND, Conductivity_Circuit1.GND, D_O_Circuit1.GND, Componente9.GND, Componente10.GND, ZS-042_RTC2.GND
  N8: DS1.DQ, Componente9.D2
  VCC: DS1.VDD, pH_Circuit1.TX, Conductivity_Circuit1.TX, D_O_Circuit1.TX, Componente9.5V, Componente10.VCC, ZS-042_RTC2.VCC
  N9: Componente9.A4/SDA, Componente10.SDA, ZS-042_RTC2.SDA
  N10: Componente9.A5/SCL, Componente10.SCL, ZS-042_RTC2.SCL
  N11: Componente9.D10_PWM/SS, microSD2.CS
  N12: Componente9.D11_PWM/MOSI, microSD2.MOSI
  N13: Componente9.D12/MISO, microSD2.MISO
  N14: Componente9.D13/SCK, microSD2.SCK

custom parts:
  : TDS Meter V1.0 Development Board Water Meter Filter Measuring Water Sensor Module.
  Turbidity Sensor Probe: Turbidity sensor probe to the DFRobot measure module.
  DFRobot SEN0189: Turbidity sensor of DFRobot SEN0189
  LCD1602-I2C: A standard character display, usually with 2x16 characters. Comes in many colors with LCM1602 IIC attached.
