# Fritzing sketch PUCE (saved by Fritzing 1.0.6)
breadboards: 3

parts:
  microSD1 = MicroSD Card Module
  ZS-042_RTC1 = ZS-042 RTC Module
  Componente1 = Arduino Uno (Rev3) - ICSP
  PIR1 = PIR sensor
  Mod1 = MQ-7 breakout
  Componente7 = BH1750
  A1 = AHT10 module
  Componente5 = Breakout Board for Electret Microphone
  Componente8 = LCD1602-I2C
  Mod2 = MQ-7 breakout
  A2 = tds-sensor-meter-v1.0_1
  U1 = Turbidity Sensor Probe [package=THT]
  U2 = DFRobot SEN0189 [package=THT]
  DS1 = DS18B20 1-Wire Temperature Sensor Probe
  pH_Circuit1 = pH Circuit
  Conductivity_Circuit1 = Conductivity Circuit
  D_O_Circuit1 = D.O. Circuit
  Componente9 = Arduino Uno (Rev3) - ICSP
  Componente10 = LCD1602-I2C
  microSD2 = MicroSD Card Module
  ZS-042_RTC2 = ZS-042 RTC Module
  Componente11 = Arduino Uno (Rev3) - ICSP
  Componente12 = LCD1602-I2C
  microSD3 = MicroSD Card Module
  ZS-042_RTC3 = ZS-042 RTC Module

nets:
  N1: microSD1.MISO, Componente1.D12/MISO
  N2: microSD1.MOSI, Componente1.D11_PWM/MOSI
  N3: microSD1.SCK, Componente1.D13/SCK
  N4: microSD1.CS, Componente1.D10_PWM/SS
  GND: ZS-042_RTC1.GND, Componente1.GND, Componente8.GND
  VCC: ZS-042_RTC1.VCC, Componente1.5V, Componente8.VCC
  N5: ZS-042_RTC1.SDA, Componente1.A4/SDA, Componente8.SDA
  N6: ZS-042_RTC1.SCL, Componente1.A5/SCL, Componente8.SCL
  VCC_2: PIR1.VDD, Componente7.VCC, A1.Pin_4, Componente11.5V, Componente12.VCC, ZS-042_RTC3.VCC
  GND_2: PIR1.GND, Componente7.GND, A1.Pin_3, Componente11.GND, Componente12.GND, ZS-042_RTC3.GND
  VCC_3: Mod1.VCC, Componente5.VCC, Mod2.VCC
  GND_3: Mod1.GND, Componente5.GND, Mod2.GND
  N7: A2.pin2, U2.P1_2
  N8: A2.pin3, U2.P1_3
  N9: U1.pin1, U2.P2_3
  N10: U1.pin2, U2.P2_2
  N11: U1.VCC, U2.P2_1
  GND_4: DS1.GND, pH_Circuit1.GND, Conductivity_Circuit1.GND, D_O_Circuit1.GND, Componente9.GND, Componente10.GND, ZS-042_RTC2.GND
  VCC_4: DS1.VDD, pH_Circuit1.TX, Conductivity_Circuit1.TX, D_O_Circuit1.TX, Componente9.5V, Componente10.VCC, ZS-042_RTC2.VCC
  N12: Componente9.A4/SDA, Componente10.SDA, ZS-042_RTC2.SDA
  N13: Componente9.A5/SCL, Componente10.SCL, ZS-042_RTC2.SCL
  N14: Componente9.D10_PWM/SS, microSD2.CS
  N15: Componente9.D11_PWM/MOSI, microSD2.MOSI
  N16: Componente9.D12/MISO, microSD2.MISO
  N17: Componente9.D13/SCK, microSD2.SCK
  N18: Componente11.A4/SDA, Componente12.SDA, ZS-042_RTC3.SDA
  N19: Componente11.A5/SCL, Componente12.SCL, ZS-042_RTC3.SCL
  N20: Componente11.D10_PWM/SS, microSD3.CS
  N21: Componente11.D11_PWM/MOSI, microSD3.MOSI
  N22: Componente11.D12/MISO, microSD3.MISO
  N23: Componente11.D13/SCK, microSD3.SCK

custom parts:
  MQ-7 breakout: MQ-5 gas sensor
  BH1750: Light Sensor
  AHT10 module: AHT10 Temperature Humidity Sensor Measurement Module High-Precision Digital Temp Humidity Sensor Measurement Module 1.8-6.0V I2C.
  LCD1602-I2C: A standard character display, usually with 2x16 characters. Comes in many colors with LCM1602 IIC attached.
  : TDS Meter V1.0 Development Board Water Meter Filter Measuring Water Sensor Module.
  Turbidity Sensor Probe: Turbidity sensor probe to the DFRobot measure module.
  DFRobot SEN0189: Turbidity sensor of DFRobot SEN0189
